// Logisim project Etapa2.circ as structural Verilog: 33 circuits, main circuit estados
module estados (
  input  RESET,
  input  A,
  input  B,
  input  C,
  input  D,
  input  E
);

  wire binary_to_bcd_converter_1_p2, binary_to_bcd_converter_1_p3, binary_to_bcd_converter_1_p4, clock_1_out,
       d0, d0_sig, d1, d1_sig, d2, d2_sig, d3, d3_sig, d4, d4_sig, d5, d5_sig, d6, d6_sig, d7, d7_sig, d8,
       d8_sig, es_0, es_5, es_31, es_62, es_95, es_124, es_372, es_475, F1, F2, F3, F4, F5, modo_alt;
  wire [8:0] multiplexer_1_out;
  wire [17:0] alternativo;

  Multiplexer #(.width(9)) multiplexer_1 (
    .in0({d0_sig, d1_sig, d2_sig, d3_sig, d4_sig, d5_sig, d6_sig, d7_sig, d8_sig}), .in1(alternativo[8:0]),
    .out(multiplexer_1_out), .sel(modo_alt));
  Clock clock_1 (.out(clock_1_out));
  Counter #(.max('h1ff), .width(9)) counter_1 (
    .clr(RESET), .load(1'b1), .clk(clock_1_out), .D(multiplexer_1_out),
    .Q({d0, d1, d2, d3, d4, d5, d6, d7, d8}));  // open: up, count, carry
  estado_sig_d0 estado_sig_d0_1 (
    .es_0(es_0), .es_124(es_124), .es_95(es_95), .es_62(es_62), .es_5(es_5), .es_372(es_372),
    .es_475(es_475), .es_31(es_31), .F1(F1), .F2(F2), .F3(F3), .F4(F4), .F5(F5), .d0_sig(d0_sig));
  estado_sig_d1 estado_sig_d1_1 (
    .es_0(es_0), .es_124(es_124), .es_95(es_95), .es_62(es_62), .es_5(es_5), .es_372(es_372),
    .es_475(es_475), .es_31(es_31), .F1(F1), .F2(F2), .F3(F3), .F4(F4), .F5(F5), .d1_sig(d1_sig));
  estado_sig_d3 estado_sig_d3_1 (
    .es_0(es_0), .es_124(es_124), .es_95(es_95), .es_62(es_62), .es_5(es_5), .es_372(es_372),
    .es_475(es_475), .es_31(es_31), .F1(F1), .F2(F2), .F3(F3), .F4(F4), .F5(F5), .d3_sig(d3_sig));
  estado_sig_d5 estado_sig_d5_1 (
    .es_0(es_0), .es_124(es_124), .es_95(es_95), .es_62(es_62), .es_5(es_5), .es_372(es_372),
    .es_475(es_475), .es_31(es_31), .F1(F1), .F2(F2), .F3(F3), .F4(F4), .F5(F5), .d5_sig(d5_sig));
  estado_sig_d8 estado_sig_d8_1 (
    .es_0(es_0), .es_124(es_124), .es_95(es_95), .es_62(es_62), .es_5(es_5), .es_372(es_372),
    .es_475(es_475), .es_31(es_31), .F1(F1), .F2(F2), .F3(F3), .F4(F4), .F5(F5), .d8_sig(d8_sig));
  // Binary_to_BCD_converter binary_to_bcd_converter_1: pin names not known; wires that end beside it: {d0, d1, d2, d3, d4, d5, d6, d7, d8}, binary_to_bcd_converter_1_p2, binary_to_bcd_converter_1_p3, binary_to_bcd_converter_1_p4
  Etapa2_Modulo etapa2_modulo_1 (.in_1({d0, d1, d2, d3, d4, d5, d6, d7, d8}), .resultado(alternativo));
  _7_Segment_Display u_7_segment_display_1 ();  // open: g, f, a, b, e, d, c, dp
  // BCD_to_7_Segment_decoder bcd_to_7_segment_decoder_1: pin names not known; wires that end beside it: binary_to_bcd_converter_1_p2
  _7_Segment_Display u_7_segment_display_2 ();  // open: g, f, a, b, e, d, c, dp
  // BCD_to_7_Segment_decoder bcd_to_7_segment_decoder_2: pin names not known; wires that end beside it: binary_to_bcd_converter_1_p3
  LED led_1 (.in(F1));
  LED led_2 (.in(F3));
  LED led_3 (.in(F4));
  _7_Segment_Display u_7_segment_display_3 ();  // open: g, f, a, b, e, d, c, dp
  // BCD_to_7_Segment_decoder bcd_to_7_segment_decoder_3: pin names not known; wires that end beside it: binary_to_bcd_converter_1_p4
  LED led_4 (.in(F2));
  LED led_5 (.in(F5));
  funciones funciones_1 (.A(A), .B(B), .C(C), .D(D), .E(E), .F1(F1), .F2(F2), .F3(F3), .F5(F5), .F4(F4));
  modo_alternativo modo_alternativo_1 (
    .es_0(es_0), .es_124(es_124), .es_95(es_95), .es_62(es_62), .es_5(es_5), .es_372(es_372),
    .es_475(es_475), .es_31(es_31), .F1(F1), .F2(F2), .F3(F3), .F4(F4), .F5(F5), .modo_alt(modo_alt));
  estado_sig_d2 estado_sig_d2_1 (
    .es_0(es_0), .es_124(es_124), .es_95(es_95), .es_62(es_62), .es_5(es_5), .es_372(es_372),
    .es_475(es_475), .es_31(es_31), .F1(F1), .F2(F2), .F3(F3), .F4(F4), .F5(F5), .d2_sig(d2_sig));
  estado_sig_d4 estado_sig_d4_1 (
    .es_0(es_0), .es_124(es_124), .es_95(es_95), .es_62(es_62), .es_5(es_5), .es_372(es_372),
    .es_475(es_475), .es_31(es_31), .F1(F1), .F2(F2), .F3(F3), .F4(F4), .F5(F5), .d4_sig(d4_sig));
  estado_sig_d6 estado_sig_d6_1 (
    .es_0(es_0), .es_124(es_124), .es_95(es_95), .es_62(es_62), .es_5(es_5), .es_372(es_372),
    .es_475(es_475), .es_31(es_31), .F1(F1), .F2(F2), .F3(F3), .F4(F4), .F5(F5), .d6_sig(d6_sig));
  estado_sig_d7 estado_sig_d7_1 (
    .es_0(es_0), .es_124(es_124), .es_95(es_95), .es_62(es_62), .es_5(es_5), .es_372(es_372),
    .es_475(es_475), .es_31(es_31), .F1(F1), .F2(F2), .F3(F3), .F4(F4), .F5(F5), .d7_sig(d7_sig));
  COMPARADOR0 comparador0_1 (
    .d0(d0), .d1(d1), .d2(d2), .d3(d3), .d4(d4), .d5(d5), .d6(d6), .d7(d7), .d8(d8), .es_0(es_0));
  COMPARADOR5 comparador5_1 (
    .d0(d0), .d1(d1), .d2(d2), .d3(d3), .d4(d4), .d5(d5), .d6(d6), .d7(d7), .d8(d8), .es_5(es_5));
  COMPARADOR475 comparador475_1 (
    .d0(d0), .d1(d1), .d2(d2), .d3(d3), .d4(d4), .d5(d5), .d6(d6), .d7(d7), .d8(d8), .es_475(es_475));
  COMPARADOR95 comparador95_1 (
    .d0(d0), .d1(d1), .d2(d2), .d3(d3), .d4(d4), .d5(d5), .d6(d6), .d7(d7), .d8(d8), .es_95(es_95));
  COMPARADOR62 comparador62_1 (
    .d0(d0), .d1(d1), .d2(d2), .d3(d3), .d4(d4), .d5(d5), .d6(d6), .d7(d7), .d8(d8), .es_62(es_62));
  COMPARADOR31 comparador31_1 (
    .d0(d0), .d1(d1), .d2(d2), .d3(d3), .d4(d4), .d5(d5), .d6(d6), .d7(d7), .d8(d8), .es_31(es_31));
  COMPARADOR124 comparador124_1 (
    .d0(d0), .d1(d1), .d2(d2), .d3(d3), .d4(d4), .d5(d5), .d6(d6), .d7(d7), .d8(d8), .es_124(es_124));
  COMPARADOR372 comparador372_1 (
    .d0(d0), .d1(d1), .d2(d2), .d3(d3), .d4(d4), .d5(d5), .d6(d6), .d7(d7), .d8(d8), .es_372(es_372));

  // Other names for the same wires on the sheet: modo_normal[8:0] = {d0_sig, d1_sig, d2_sig, d3_sig, d4_sig, d5_sig, d6_sig, d7_sig, d8_sig}

  // Notes on the sheet:
  //   ESTADO ACTUAL
endmodule

module funciones (
  input  A,
  input  B,
  input  C,
  input  D,
  input  E,
  output F1,
  output F2,
  output F3,
  output F5,
  output F4
);

  wire and_1_out, and_2_out, and_3_out, and_4_out, and_5_out, and_6_out, and_7_out, and_8_out, and_9_out,
       and_10_out, and_11_out, and_12_out, and_13_out, and_14_out, and_15_out, and_16_out, and_17_out,
       and_18_out, and_19_out, and_20_out, and_21_out, and_22_out, and_23_out, and_24_out, and_25_out,
       and_26_out, and_27_out, CnoDnoE_out, CyDyE, decoder_1_out0, decoder_1_out2, decoder_1_out4,
       decoder_1_out7, decoder_1_out11, decoder_1_out12, decoder_1_out13, decoder_1_out15, decoder_1_out20,
       nCDE, noC, noE, not_3_out, not_4_out, not_5_out, not_6_out, not_7_out, not_8_out, or_1_out, or_2_out,
       or_3_out, or_4_out, or_6_out, or_7_out, or_8_out, or_9_out, or_10_out, or_11_out, or_12_out,
       or_13_out, or_14_out, or_16_out, or_17_out;

  not not_1 (noE, E);
  not not_2 (noC, C);
  not not_3 (not_3_out, D);
  not not_4 (not_4_out, A);
  not not_5 (not_5_out, B);
  not not_6 (not_6_out, C);
  not not_7 (not_7_out, D);
  not not_8 (not_8_out, E);
  and and_1 (and_1_out, A, not_5_out);
  and and_2 (and_2_out, and_1_out, C);
  and and_3 (and_3_out, not_7_out, E);
  and and_4 (and_4_out, A, B);
  and and_5 (and_5_out, and_4_out, not_6_out);
  and and_6 (and_6_out, not_7_out, E);
  and and_7 (and_7_out, not_4_out, B);
  and and_8 (and_8_out, C, not_7_out);
  and and_9 (and_9_out, A, B);
  and and_10 (and_10_out, and_9_out, C);
  and and_11 (and_11_out, D, E);
  and and_12 (and_12_out, and_2_out, and_3_out);
  and and_13 (and_13_out, and_5_out, and_6_out);
  and and_14 (and_14_out, not_4_out, B);
  and and_15 (and_15_out, not_6_out, D);
  and and_16 (and_16_out, and_7_out, and_8_out);
  and and_17 (and_17_out, and_10_out, and_11_out);
  and and_18 (and_18_out, not_4_out, B);
  and and_19 (and_19_out, D, not_8_out);
  Decoder #(.enable("false"), .select(5)) decoder_1 (
    .out0(decoder_1_out0), .out2(decoder_1_out2), .out4(decoder_1_out4), .out7(decoder_1_out7),
    .out11(decoder_1_out11), .out12(decoder_1_out12), .out13(decoder_1_out13), .out15(decoder_1_out15),
    .out20(decoder_1_out20), .sel({A, B, C, D, E}));  // open: out1, out3, out5, out6, out8, out9, out10, out14, out16, out17, out18, out19, out21, out22, out23, out24, out25, out26, out27, out28, out29, out30, out31
  and noCDE (nCDE, noC, D, E);
  and and_20 (and_20_out, noC, D);
  and and_21 (and_21_out, not_3_out, C);
  and and_22 (and_22_out, not_3_out, noC, noE);
  or or_1 (or_1_out, and_12_out, and_13_out);
  and and_23 (and_23_out, and_14_out, and_15_out);
  or or_2 (or_2_out, and_16_out, and_17_out);
  and and_24 (and_24_out, and_18_out, and_19_out);
  and CnoDnoE (CnoDnoE_out, C, not_3_out, noE);
  and CDE (CyDyE, C, D, E);
  or or_3 (or_3_out, or_1_out, and_23_out);
  or or_4 (or_4_out, or_2_out, and_24_out);
  and and_25 (and_25_out, C, E);
  and and_26 (and_26_out, not_3_out, noE);
  or or_5 (F5, or_3_out, or_4_out);
  or or_6 (or_6_out, and_21_out, nCDE);
  and and_27 (and_27_out, noC, D, noE);
  or or_7 (or_7_out, decoder_1_out0, decoder_1_out2, decoder_1_out4, decoder_1_out7);
  or or_8 (or_8_out, decoder_1_out11, decoder_1_out12, decoder_1_out13);
  or or_9 (or_9_out, decoder_1_out15, decoder_1_out20);
  or or_10 (or_10_out, and_25_out, and_26_out);
  or or_11 (or_11_out, and_25_out, and_20_out);
  or or_12 (or_12_out, nCDE, CnoDnoE_out, CyDyE);
  or or_13 (or_13_out, CnoDnoE_out, and_27_out);
  or or_14 (or_14_out, or_7_out, or_8_out);
  or or_15 (F4, or_14_out, or_9_out);
  Multiplexer #(.select(2)) multiplexer_1 (
    .in0(nCDE), .in1(or_12_out), .in2(or_10_out), .in3(and_26_out), .out(F1), .sel({A, B}));
  or or_16 (or_16_out, nCDE, CyDyE);
  or or_17 (or_17_out, nCDE, CyDyE, and_26_out);
  Multiplexer #(.select(2)) multiplexer_2 (
    .in0(and_26_out), .in1(or_11_out), .in2(or_17_out), .in3(or_16_out), .out(F2), .sel({A, B}));
  Multiplexer #(.select(2)) multiplexer_3 (
    .in0(or_6_out), .in1(and_22_out), .in2(or_13_out), .in3(or_6_out), .out(F3), .sel({A, B}));
endmodule

module estado_sig_d0 (
  input  es_0,
  input  es_124,
  input  es_95,
  input  es_62,
  input  es_5,
  input  es_372,
  input  es_475,
  input  es_31,
  input  F1,
  input  F2,
  input  F3,
  input  F4,
  input  F5,
  output d0_sig
);

  wire nof4y5_out, not_1_out;

  not not_1 (not_1_out, F4);
  and nof4y5 (nof4y5_out, not_1_out, es_5);
  or or_1 (d0_sig, es_372, nof4y5_out);
endmodule

module estado_sig_d1 (
  input  es_0,
  input  es_124,
  input  es_95,
  input  es_62,
  input  es_5,
  input  es_372,
  input  es_475,
  input  es_31,
  input  F1,
  input  F2,
  input  F3,
  input  F4,
  input  F5,
  output d1_sig
);


  assign d1_sig = es_372;
endmodule

module estado_sig_d2 (
  input  es_0,
  input  es_124,
  input  es_95,
  input  es_62,
  input  es_5,
  input  es_372,
  input  es_475,
  input  es_31,
  input  F1,
  input  F2,
  input  F3,
  input  F4,
  input  F5,
  output d2_sig
);

  wire nof1y124_out, nof4y5_out, not_1_out, not_2_out;

  not not_1 (not_1_out, F1);
  not not_2 (not_2_out, F4);
  and nof4y5 (nof4y5_out, es_5, not_2_out);
  and nof1y124 (nof1y124_out, es_124, not_1_out);
  or or_1 (d2_sig, nof1y124_out, es_0, nof4y5_out, es_372);
endmodule

module estado_sig_d3 (
  input  es_0,
  input  es_124,
  input  es_95,
  input  es_62,
  input  es_5,
  input  es_372,
  input  es_475,
  input  es_31,
  input  F1,
  input  F2,
  input  F3,
  input  F4,
  input  F5,
  output d3_sig
);

  wire nof2y95_out, nof4y5_out, not_1_out, not_2_out;

  not not_1 (not_1_out, F2);
  not not_2 (not_2_out, F4);
  and nof2y95 (nof2y95_out, es_95, not_1_out);
  and nof4y5 (nof4y5_out, es_5, not_2_out);
  or or_1 (d3_sig, es_0, nof4y5_out, nof2y95_out);
endmodule

module estado_sig_d4 (
  input  es_0,
  input  es_124,
  input  es_95,
  input  es_62,
  input  es_5,
  input  es_372,
  input  es_475,
  input  es_31,
  input  F1,
  input  F2,
  input  F3,
  input  F4,
  input  F5,
  output d4_sig
);

  wire nof1y124_out, nof2y95_out, nof4y5_out, nof4y475_out, not_1_out, not_2_out, not_3_out, or_1_out,
       or_2_out;

  not not_1 (not_1_out, F1);
  not not_2 (not_2_out, F2);
  not not_3 (not_3_out, F4);
  and nof1y124 (nof1y124_out, es_124, not_1_out);
  and nof2y95 (nof2y95_out, es_95, not_2_out);
  and nof4y5 (nof4y5_out, not_3_out, es_5);
  or or_1 (or_1_out, es_0, nof1y124_out);
  or or_2 (or_2_out, nof2y95_out, nof4y5_out, es_372);
  and nof4y475 (nof4y475_out, es_475, not_3_out);
  or or_3 (d4_sig, or_1_out, or_2_out, nof4y475_out, es_372);
endmodule

module estado_sig_d5 (
  input  es_0,
  input  es_124,
  input  es_95,
  input  es_62,
  input  es_5,
  input  es_372,
  input  es_475,
  input  es_31,
  input  F1,
  input  F2,
  input  F3,
  input  F4,
  input  F5,
  output d5_sig
);

  wire nof1y124_out, nof2y95_out, nof4y475_out, not_1_out, not_2_out, not_3_out, or_1_out;

  not not_1 (not_1_out, F1);
  not not_2 (not_2_out, F2);
  not not_3 (not_3_out, F4);
  and nof1y124 (nof1y124_out, es_124, not_1_out);
  and nof2y95 (nof2y95_out, es_95, not_2_out);
  or or_1 (or_1_out, es_0, nof1y124_out, nof2y95_out);
  and nof4y475 (nof4y475_out, es_475, not_3_out);
  or or_2 (d5_sig, or_1_out, es_372, nof4y475_out);
endmodule

module estado_sig_d6 (
  input  es_0,
  input  es_124,
  input  es_95,
  input  es_62,
  input  es_5,
  input  es_372,
  input  es_475,
  input  es_31,
  input  F1,
  input  F2,
  input  F3,
  input  F4,
  input  F5,
  output d6_sig
);

  wire no3y62_out, no4y5_out, nof1y124_out, nof2y95_out, nof4y475_out, not_1_out, not_2_out, not_3_out,
       not_4_out, or_1_out, or_2_out;

  not not_1 (not_1_out, F1);
  not not_2 (not_2_out, F2);
  not not_3 (not_3_out, F3);
  not not_4 (not_4_out, F4);
  and nof1y124 (nof1y124_out, es_124, not_1_out);
  and nof2y95 (nof2y95_out, es_95, not_2_out);
  and no3y62 (no3y62_out, es_62, not_3_out);
  and nof4y475 (nof4y475_out, es_475, not_4_out);
  and no4y5 (no4y5_out, not_4_out, es_5);
  or or_1 (or_1_out, es_0, nof1y124_out, no3y62_out);
  or or_2 (or_2_out, or_1_out, nof2y95_out, no4y5_out);
  or or_3 (d6_sig, or_2_out, nof4y475_out);
endmodule

module estado_sig_d7 (
  input  es_0,
  input  es_124,
  input  es_95,
  input  es_62,
  input  es_5,
  input  es_372,
  input  es_475,
  input  es_31,
  input  F1,
  input  F2,
  input  F3,
  input  F4,
  input  F5,
  output d7_sig
);

  wire no2y95_out, no4y475_out, nof1y124_out, not_1_out, not_2_out, not_3_out;

  not not_1 (not_1_out, F1);
  not not_2 (not_2_out, F2);
  not not_3 (not_3_out, F4);
  and nof1y124 (nof1y124_out, es_124, not_1_out);
  and no2y95 (no2y95_out, es_95, not_2_out);
  and no4y475 (no4y475_out, es_475, not_3_out);
  or or_1 (d7_sig, nof1y124_out, no2y95_out, es_372, no4y475_out);
endmodule

module estado_sig_d8 (
  input  es_0,
  input  es_124,
  input  es_95,
  input  es_62,
  input  es_5,
  input  es_372,
  input  es_475,
  input  es_31,
  input  F1,
  input  F2,
  input  F3,
  input  F4,
  input  F5,
  output d8_sig
);

  wire nof1y124_out, nof3y62_out, nof4y475_out, not_1_out, not_2_out, not_3_out;

  not not_1 (not_1_out, F1);
  not not_2 (not_2_out, F3);
  not not_3 (not_3_out, F4);
  and nof1y124 (nof1y124_out, es_124, not_1_out);
  and nof3y62 (nof3y62_out, es_62, not_2_out);
  and nof4y475 (nof4y475_out, es_475, not_3_out);
  or or_1 (d8_sig, nof1y124_out, nof3y62_out, nof4y475_out, es_372);
endmodule

module COMPARADOR0 (
  input  d0,
  input  d1,
  input  d2,
  input  d3,
  input  d4,
  input  d5,
  input  d6,
  input  d7,
  input  d8,
  output es_0
);

  wire and_1_out, and_2_out, not_1_out, not_2_out, not_3_out, not_4_out, not_5_out, not_6_out, not_7_out,
       not_8_out, not_9_out;

  not not_1 (not_1_out, d0);
  not not_2 (not_2_out, d1);
  not not_3 (not_3_out, d2);
  not not_4 (not_4_out, d3);
  not not_5 (not_5_out, d4);
  not not_6 (not_6_out, d5);
  not not_7 (not_7_out, d6);
  not not_8 (not_8_out, d7);
  not not_9 (not_9_out, d8);
  and and_1 (and_1_out, not_6_out, not_7_out, not_8_out, not_9_out);
  and and_2 (and_2_out, not_1_out, not_2_out, not_3_out, not_4_out, not_5_out);
  and and_3 (es_0, and_2_out, and_1_out);
endmodule

module COMPARADOR124 (
  input  d0,
  input  d1,
  input  d2,
  input  d3,
  input  d4,
  input  d5,
  input  d6,
  input  d7,
  input  d8,
  output es_124
);

  wire and_1_out, and_2_out, and_3_out, not_1_out, not_2_out, not_3_out, not_4_out, not_5_out, not_6_out,
       not_7_out, not_8_out, not_9_out;

  not not_1 (not_1_out, d0);
  not not_2 (not_2_out, d1);
  not not_3 (not_3_out, d2);
  not not_4 (not_4_out, d3);
  not not_5 (not_5_out, d4);
  not not_6 (not_6_out, d5);
  not not_7 (not_7_out, d6);
  not not_8 (not_8_out, d7);
  not not_9 (not_9_out, d8);
  and and_1 (and_1_out, not_1_out, not_2_out);
  and and_2 (and_2_out, d2, d3, d4, d5, d6);
  and and_3 (and_3_out, not_8_out, not_9_out);
  and and_4 (es_124, and_1_out, and_2_out, and_3_out);
endmodule

module COMPARADOR95 (
  input  d0,
  input  d1,
  input  d2,
  input  d3,
  input  d4,
  input  d5,
  input  d6,
  input  d7,
  input  d8,
  output es_95
);

  wire and_1_out, and_2_out, not_1_out, not_2_out, not_3_out, not_4_out, not_5_out, not_6_out, not_7_out,
       not_8_out, not_9_out;

  not not_1 (not_1_out, d0);
  not not_2 (not_2_out, d1);
  not not_3 (not_3_out, d2);
  not not_4 (not_4_out, d3);
  not not_5 (not_5_out, d4);
  not not_6 (not_6_out, d5);
  not not_7 (not_7_out, d6);
  not not_8 (not_8_out, d7);
  not not_9 (not_9_out, d8);
  and and_1 (and_1_out, not_1_out, not_2_out);
  and and_2 (and_2_out, d4, d5, d6, d7, d8);
  and and_3 (es_95, and_1_out, d2, not_4_out, and_2_out);
endmodule

module COMPARADOR62 (
  input  d0,
  input  d1,
  input  d2,
  input  d3,
  input  d4,
  input  d5,
  input  d6,
  input  d7,
  input  d8,
  output es_62
);

  wire and_1_out, and_2_out, not_1_out, not_2_out, not_3_out, not_4_out, not_5_out, not_6_out, not_7_out,
       not_8_out, not_9_out;

  not not_1 (not_1_out, d0);
  not not_2 (not_2_out, d1);
  not not_3 (not_3_out, d2);
  not not_4 (not_4_out, d3);
  not not_5 (not_5_out, d4);
  not not_6 (not_6_out, d5);
  not not_7 (not_7_out, d6);
  not not_8 (not_8_out, d7);
  not not_9 (not_9_out, d8);
  and and_1 (and_1_out, not_1_out, not_2_out, not_3_out);
  and and_2 (and_2_out, d3, d4, d5, d6, d7);
  and and_3 (es_62, and_1_out, and_2_out, not_9_out);
endmodule

module COMPARADOR5 (
  input  d0,
  input  d1,
  input  d2,
  input  d3,
  input  d4,
  input  d5,
  input  d6,
  input  d7,
  input  d8,
  output es_5
);

  wire and_1_out, not_1_out, not_2_out, not_3_out, not_4_out, not_5_out, not_6_out, not_7_out, not_8_out,
       not_9_out;

  not not_1 (not_1_out, d0);
  not not_2 (not_2_out, d1);
  not not_3 (not_3_out, d2);
  not not_4 (not_4_out, d3);
  not not_5 (not_5_out, d4);
  not not_6 (not_6_out, d5);
  not not_7 (not_7_out, d6);
  not not_8 (not_8_out, d7);
  not not_9 (not_9_out, d8);
  and and_1 (and_1_out, not_1_out, not_2_out, not_3_out, not_4_out, not_5_out, not_6_out);
  and and_2 (es_5, and_1_out, d6, not_8_out, d8);
endmodule

module COMPARADOR372 (
  input  d0,
  input  d1,
  input  d2,
  input  d3,
  input  d4,
  input  d5,
  input  d6,
  input  d7,
  input  d8,
  output es_372
);

  wire and_1_out, and_2_out, not_1_out, not_2_out, not_3_out, not_4_out, not_5_out, not_6_out, not_7_out,
       not_8_out, not_9_out;

  not not_1 (not_1_out, d0);
  not not_2 (not_2_out, d1);
  not not_3 (not_3_out, d2);
  not not_4 (not_4_out, d3);
  not not_5 (not_5_out, d4);
  not not_6 (not_6_out, d5);
  not not_7 (not_7_out, d6);
  not not_8 (not_8_out, d7);
  not not_9 (not_9_out, d8);
  and and_1 (and_1_out, d0, d2, d3, d4, d6);
  and and_2 (and_2_out, not_2_out, not_6_out, not_8_out, not_9_out);
  and and_3 (es_372, and_1_out, and_2_out);
endmodule

module COMPARADOR475 (
  input  d0,
  input  d1,
  input  d2,
  input  d3,
  input  d4,
  input  d5,
  input  d6,
  input  d7,
  input  d8,
  output es_475
);

  wire and_1_out, and_2_out, not_1_out, not_2_out, not_3_out, not_4_out, not_5_out, not_6_out, not_7_out,
       not_8_out, not_9_out;

  not not_1 (not_1_out, d0);
  not not_2 (not_2_out, d1);
  not not_3 (not_3_out, d2);
  not not_4 (not_4_out, d3);
  not not_5 (not_5_out, d4);
  not not_6 (not_6_out, d5);
  not not_7 (not_7_out, d6);
  not not_8 (not_8_out, d7);
  not not_9 (not_9_out, d8);
  and and_1 (and_1_out, d0, d1, d2, d4, d5, d7, d8);
  and and_2 (and_2_out, not_4_out, not_7_out);
  and and_3 (es_475, and_1_out, and_2_out);
endmodule

module COMPARADOR31 (
  input  d0,
  input  d1,
  input  d2,
  input  d3,
  input  d4,
  input  d5,
  input  d6,
  input  d7,
  input  d8,
  output es_31
);

  wire and_1_out, and_2_out, not_1_out, not_2_out, not_3_out, not_4_out, not_5_out, not_6_out, not_7_out,
       not_8_out, not_9_out;

  not not_1 (not_1_out, d0);
  not not_2 (not_2_out, d1);
  not not_3 (not_3_out, d2);
  not not_4 (not_4_out, d3);
  not not_5 (not_5_out, d4);
  not not_6 (not_6_out, d5);
  not not_7 (not_7_out, d6);
  not not_8 (not_8_out, d7);
  not not_9 (not_9_out, d8);
  and and_1 (and_1_out, not_1_out, not_2_out, not_3_out, not_4_out);
  and and_2 (and_2_out, d4, d5, d6, d7, d8);
  and and_3 (es_31, and_1_out, and_2_out);
endmodule

module Etapa2_Modulo (
  input  [8:0] in_1,
  output [17:0] resultado
);

  wire [8:0] factor_1_output_factor;

  Factor factor_1 (.Input_Factor(in_1), .Output_Factor(factor_1_output_factor));
  MultiplicadorAC multiplicadorac_1 (
    .op1_9bits(in_1), .op2_9bits(factor_1_output_factor), .res_18bits(resultado));  // open: carry_out

  // Notes on the sheet:
  //   Estado Actual
  //   MODO ALTERNATIVO
  //   Operando 2
  //   Operando 1
  //   Multiplicador de 9 bits
endmodule

module Factor (
  input  [8:0] Input_Factor,
  output [8:0] Output_Factor
);

  ROM #(.addrWidth(9), .dataWidth(9)) rom_1 (.addr(Input_Factor), .data(Output_Factor));

  // Notes on the sheet:
  //   contents of rom_1 (hex, n*v repeats v):
  //   5*0 1 25*0 4 30*0 6 32*0 5 28*0 3 350*0 1
endmodule

module MultiplicadorAC (
  input  [8:0] op1_9bits,
  input  [8:0] op2_9bits,
  output carry_out,
  output [17:0] res_18bits
);

  wire [17:0] calculo_productos_parciales_1_op1_op2_0, calculo_productos_parciales_1_op1_op2_1,
       calculo_productos_parciales_1_op1_op2_2, calculo_productos_parciales_1_op1_op2_3,
       calculo_productos_parciales_1_op1_op2_4, calculo_productos_parciales_1_op1_op2_5,
       calculo_productos_parciales_1_op1_op2_6, calculo_productos_parciales_1_op1_op2_7,
       calculo_productos_parciales_1_op1_op2_8, csa_1_sc, csa_1_ss, csa_2_sc, csa_2_ss, csa_3_sc, csa_3_ss,
       csa_4_sc, csa_4_ss, csa_5_sc, csa_5_ss, csa_6_sc, csa_6_ss, csa_7_sc, csa_7_ss, shifter_1_out,
       shifter_2_out, shifter_3_out, shifter_4_out, shifter_5_out, shifter_6_out, shifter_7_out;

  calculo_productos_parciales calculo_productos_parciales_1 (
    .operador1(op1_9bits), .operador2(op2_9bits), .op1_op2_0(calculo_productos_parciales_1_op1_op2_0),
    .op1_op2_1(calculo_productos_parciales_1_op1_op2_1), .op1_op2_2(calculo_productos_parciales_1_op1_op2_2),
    .op1_op2_3(calculo_productos_parciales_1_op1_op2_3), .op1_op2_4(calculo_productos_parciales_1_op1_op2_4),
    .op1_op2_5(calculo_productos_parciales_1_op1_op2_5), .op1_op2_6(calculo_productos_parciales_1_op1_op2_6),
    .op1_op2_7(calculo_productos_parciales_1_op1_op2_7), .op1_op2_8(calculo_productos_parciales_1_op1_op2_8));
  CSA csa_1 (
    .Z(calculo_productos_parciales_1_op1_op2_8), .X(calculo_productos_parciales_1_op1_op2_7),
    .Y(calculo_productos_parciales_1_op1_op2_6), .ss(csa_1_ss), .sc(csa_1_sc));
  Shifter #(.width(18)) shifter_1 (.in(csa_1_sc), .\dist (5'b00001), .out(shifter_1_out));
  CSA csa_2 (
    .Z(csa_1_ss), .X(shifter_1_out), .Y(calculo_productos_parciales_1_op1_op2_5), .ss(csa_2_ss), .sc(csa_2_sc));
  Shifter #(.width(18)) shifter_2 (.in(csa_3_sc), .\dist (5'b00001), .out(shifter_2_out));
  Shifter #(.width(18)) shifter_3 (.in(csa_2_sc), .\dist (5'b00001), .out(shifter_3_out));
  Shifter #(.width(18)) shifter_4 (.in(csa_4_sc), .\dist (5'b00001), .out(shifter_4_out));
  CSA csa_3 (
    .Z(csa_2_ss), .X(shifter_3_out), .Y(calculo_productos_parciales_1_op1_op2_4), .ss(csa_3_ss), .sc(csa_3_sc));
  CSA csa_4 (
    .Z(shifter_2_out), .X(csa_3_ss), .Y(calculo_productos_parciales_1_op1_op2_3), .ss(csa_4_ss), .sc(csa_4_sc));
  Shifter #(.width(18)) shifter_5 (.in(csa_5_sc), .\dist (5'b00001), .out(shifter_5_out));
  Shifter #(.width(18)) shifter_6 (.in(csa_6_sc), .\dist (5'b00001), .out(shifter_6_out));
  CSA csa_5 (
    .Z(shifter_4_out), .X(csa_4_ss), .Y(calculo_productos_parciales_1_op1_op2_2), .ss(csa_5_ss), .sc(csa_5_sc));
  CSA csa_6 (
    .Z(csa_5_ss), .X(shifter_5_out), .Y(calculo_productos_parciales_1_op1_op2_1), .ss(csa_6_ss), .sc(csa_6_sc));
  CSA csa_7 (
    .Z(csa_6_ss), .X(shifter_6_out), .Y(calculo_productos_parciales_1_op1_op2_0), .ss(csa_7_ss), .sc(csa_7_sc));
  Shifter #(.width(18)) shifter_7 (.in(csa_7_sc), .\dist (5'b00001), .out(shifter_7_out));
  CARRY_SKIP_ADDER carry_skip_adder_1 (
    .X(csa_7_ss), .Y(shifter_7_out), .carry_out(carry_out), .SUMA(res_18bits));  // open: c0
endmodule

module FULL_ADDER (
  input  A,
  input  B,
  input  C,
  output S,
  output C_OUT
);

  wire and_1_out, and_2_out, or_1_out, xor_1_out;

  xor xor_1 (xor_1_out, A, B);
  or or_1 (or_1_out, A, B);
  and and_1 (and_1_out, B, A);
  xor xor_2 (S, xor_1_out, C);
  and and_2 (and_2_out, C, or_1_out);
  or or_2 (C_OUT, and_2_out, and_1_out);
endmodule

module CSA (
  input  [17:0] Z,
  input  [17:0] X,
  input  [17:0] Y,
  output [17:0] ss,
  output [17:0] sc
);

  FULL_ADDER b0 (.A(X[17]), .B(Y[17]), .C(Z[17]), .S(ss[17]), .C_OUT(sc[17]));
  FULL_ADDER b1 (.A(X[16]), .B(Y[16]), .C(Z[16]), .S(ss[16]), .C_OUT(sc[16]));
  FULL_ADDER b2 (.A(X[15]), .B(Y[15]), .C(Z[15]), .S(ss[15]), .C_OUT(sc[15]));
  FULL_ADDER b9 (.A(X[8]), .B(Y[8]), .C(Z[8]), .S(ss[8]), .C_OUT(sc[8]));
  FULL_ADDER b11 (.A(X[6]), .B(Y[6]), .C(Z[6]), .S(ss[6]), .C_OUT(sc[6]));
  FULL_ADDER b15 (.A(X[2]), .B(Y[2]), .C(Z[2]), .S(ss[2]), .C_OUT(sc[2]));
  FULL_ADDER b3 (.A(X[14]), .B(Y[14]), .C(Z[14]), .S(ss[14]), .C_OUT(sc[14]));
  FULL_ADDER b4 (.A(X[13]), .B(Y[13]), .C(Z[13]), .S(ss[13]), .C_OUT(sc[13]));
  FULL_ADDER b5 (.A(X[12]), .B(Y[12]), .C(Z[12]), .S(ss[12]), .C_OUT(sc[12]));
  FULL_ADDER b10 (.A(X[7]), .B(Y[7]), .C(Z[7]), .S(ss[7]), .C_OUT(sc[7]));
  FULL_ADDER b13 (.A(X[4]), .B(Y[4]), .C(Z[4]), .S(ss[4]), .C_OUT(sc[4]));
  FULL_ADDER b16 (.A(X[1]), .B(Y[1]), .C(Z[1]), .S(ss[1]), .C_OUT(sc[1]));
  FULL_ADDER b6 (.A(X[11]), .B(Y[11]), .C(Z[11]), .S(ss[11]), .C_OUT(sc[11]));
  FULL_ADDER b7 (.A(X[10]), .B(Y[10]), .C(Z[10]), .S(ss[10]), .C_OUT(sc[10]));
  FULL_ADDER b8 (.A(X[9]), .B(Y[9]), .C(Z[9]), .S(ss[9]), .C_OUT(sc[9]));
  FULL_ADDER b12 (.A(X[5]), .B(Y[5]), .C(Z[5]), .S(ss[5]), .C_OUT(sc[5]));
  FULL_ADDER b14 (.A(X[3]), .B(Y[3]), .C(Z[3]), .S(ss[3]), .C_OUT(sc[3]));
  FULL_ADDER b17 (.A(X[0]), .B(Y[0]), .C(Z[0]), .S(ss[0]), .C_OUT(sc[0]));

  // Other names for the same wires on the sheet: c17 = sc[0]; c16 = sc[1]; c15 = sc[2]; c14 = sc[3]; c13 = sc[4];
  //   c12 = sc[5]; c11 = sc[6]; c10 = sc[7]; c9 = sc[8]; c8 = sc[9]; c7 = sc[10]; c6 = sc[11]; c5 = sc[12];
  //   c4 = sc[13]; c3 = sc[14]; c2 = sc[15]; c1 = sc[16]; c0 = sc[17]; s17 = ss[0]; s16 = ss[1]; s15 = ss[2];
  //   s14 = ss[3]; s13 = ss[4]; s12 = ss[5]; s11 = ss[6]; s10 = ss[7]; s9 = ss[8]; s8 = ss[9]; s7 = ss[10];
  //   s6 = ss[11]; s5 = ss[12]; s4 = ss[13]; s3 = ss[14]; s2 = ss[15]; s1 = ss[16]; s0 = ss[17]; x_17 = X[0];
  //   x_16 = X[1]; x_15 = X[2]; x_14 = X[3]; x_13 = X[4]; x_12 = X[5]; x_11 = X[6]; x_10 = X[7]; x_9 = X[8];
  //   x_8 = X[9]; x_7 = X[10]; x_6 = X[11]; x_5 = X[12]; x_4 = X[13]; x_3 = X[14]; x_2 = X[15]; x_1 = X[16];
  //   x_0 = X[17]; y_17 = Y[0]; y_16 = Y[1]; y_15 = Y[2]; y_14 = Y[3]; y_13 = Y[4]; y_12 = Y[5]; y_11 = Y[6];
  //   y_10 = Y[7]; y_9 = Y[8]; y_8 = Y[9]; y_7 = Y[10]; y_6 = Y[11]; y_5 = Y[12]; y_4 = Y[13]; y_3 = Y[14];
  //   y_2 = Y[15]; y_1 = Y[16]; y_0 = Y[17]; z_17 = Z[0]; z_16 = Z[1]; z_15 = Z[2]; z_14 = Z[3]; z_13 = Z[4];
  //   z_12 = Z[5]; z_11 = Z[6]; z_10 = Z[7]; z_9 = Z[8]; z_8 = Z[9]; z_7 = Z[10]; z_6 = Z[11]; z_5 = Z[12];
  //   z_4 = Z[13]; z_3 = Z[14]; z_2 = Z[15]; z_1 = Z[16]; z_0 = Z[17]
endmodule

module productos_parciales (
  input  [8:0] A,
  input  \bit ,
  output [17:0] res
);

  and b0 (res[8], A[8], \bit );
  and b1 (res[7], A[7], \bit );
  and b2 (res[6], A[6], \bit );
  and b3 (res[5], A[5], \bit );
  and b4 (res[4], A[4], \bit );
  and b5 (res[3], A[3], \bit );
  and b6 (res[2], \bit , A[2]);
  and b7 (res[1], A[1], \bit );
  and b8 (res[0], A[0], \bit );

  assign res[17:9] = {9{1'b0}};

  // Other names for the same wires on the sheet: b8 = res[0]; b7 = res[1]; b6 = res[2]; b5 = res[3]; b4 = res[4];
  //   b3 = res[5]; b2 = res[6]; b1 = res[7]; b0 = res[8]
endmodule

module calculo_productos_parciales (
  input  [8:0] operador1,
  input  [8:0] operador2,
  output [17:0] op1_op2_0,
  output [17:0] op1_op2_1,
  output [17:0] op1_op2_2,
  output [17:0] op1_op2_3,
  output [17:0] op1_op2_4,
  output [17:0] op1_op2_5,
  output [17:0] op1_op2_6,
  output [17:0] op1_op2_7,
  output [17:0] op1_op2_8
);

  wire [17:0] productos_parciales_1_res, productos_parciales_2_res, productos_parciales_3_res,
       productos_parciales_4_res, productos_parciales_5_res, productos_parciales_6_res,
       productos_parciales_7_res, productos_parciales_8_res;

  productos_parciales productos_parciales_1 (.A(operador1), .\bit (operador2[8]), .res(productos_parciales_1_res));
  productos_parciales productos_parciales_2 (.A(operador1), .\bit (operador2[7]), .res(productos_parciales_2_res));
  productos_parciales productos_parciales_3 (.A(operador1), .\bit (operador2[6]), .res(productos_parciales_3_res));
  productos_parciales productos_parciales_4 (.A(operador1), .\bit (operador2[5]), .res(productos_parciales_4_res));
  productos_parciales productos_parciales_5 (.A(operador1), .\bit (operador2[4]), .res(productos_parciales_5_res));
  productos_parciales productos_parciales_6 (.A(operador1), .\bit (operador2[3]), .res(productos_parciales_6_res));
  productos_parciales productos_parciales_7 (.A(operador1), .\bit (operador2[2]), .res(productos_parciales_7_res));
  productos_parciales productos_parciales_8 (.A(operador1), .\bit (operador2[1]), .res(productos_parciales_8_res));
  productos_parciales productos_parciales_9 (.A(operador1), .\bit (operador2[0]), .res(op1_op2_8));
  Shifter #(.width(18)) shifter_1 (.in(productos_parciales_1_res), .\dist (5'b01000), .out(op1_op2_0));
  Shifter #(.width(18)) shifter_2 (.in(productos_parciales_2_res), .\dist (5'b00111), .out(op1_op2_1));
  Shifter #(.width(18)) shifter_3 (.in(productos_parciales_3_res), .\dist (5'b00110), .out(op1_op2_2));
  Shifter #(.width(18)) shifter_4 (.in(productos_parciales_4_res), .\dist (5'b00101), .out(op1_op2_3));
  Shifter #(.width(18)) shifter_5 (.in(productos_parciales_5_res), .\dist (5'b00100), .out(op1_op2_4));
  Shifter #(.width(18)) shifter_6 (.in(productos_parciales_6_res), .\dist (5'b00011), .out(op1_op2_5));
  Shifter #(.width(18)) shifter_7 (.in(productos_parciales_7_res), .\dist (5'b00010), .out(op1_op2_6));
  Shifter #(.width(18)) shifter_8 (.in(productos_parciales_8_res), .\dist (5'b00001), .out(op1_op2_7));

  // Other names for the same wires on the sheet: d8 = operador2[0]; d7 = operador2[1]; d6 = operador2[2];
  //   d5 = operador2[3]; d4 = operador2[4]; d3 = operador2[5]; d2 = operador2[6]; d1 = operador2[7];
  //   d0 = operador2[8]
endmodule

module CARRY_SKIP_ADDER (
  input  c0,
  input  [17:0] X,
  input  [17:0] Y,
  output carry_out,
  output [17:0] SUMA
);

  wire and_1_out, and_2_out, bloque_3_1_carry_bloque3, bloque_4_1_carry_bloque4, bloque_4_1_p,
       bloque_5_1_carry_bloque6, bloque_5_1_p, or_1_out, or_2_out;

  bloque_3 bloque_3_1 (
    .c0(c0), .a0(X[0]), .b0(Y[0]), .a1(X[1]), .b1(Y[1]), .a2(X[2]), .b2(Y[2]),
    .carry_bloque3(bloque_3_1_carry_bloque3), .Ss(SUMA[2:0]));  // open: P
  bloque_4 bloque_4_1 (
    .c0(bloque_3_1_carry_bloque3), .a0(X[3]), .b0(Y[3]), .a1(X[4]), .b1(Y[4]), .a2(X[5]), .b2(Y[5]),
    .a3(X[6]), .b3(Y[6]), .carry_bloque4(bloque_4_1_carry_bloque4), .Ss(SUMA[6:3]), .P(bloque_4_1_p));
  and and_1 (and_1_out, bloque_3_1_carry_bloque3, bloque_4_1_p);
  or or_1 (or_1_out, bloque_4_1_carry_bloque4, and_1_out);
  bloque_5 bloque_5_1 (
    .c0(or_1_out), .a0(X[7]), .b0(Y[7]), .a1(X[8]), .b1(Y[8]), .a2(X[9]), .b2(Y[9]), .a3(X[10]), .b3(Y[10]),
    .a4(X[11]), .b4(Y[11]), .carry_bloque6(bloque_5_1_carry_bloque6), .Ss(SUMA[11:7]), .P(bloque_5_1_p));
  or or_2 (or_2_out, and_2_out, bloque_5_1_carry_bloque6);
  and and_2 (and_2_out, bloque_4_1_carry_bloque4, bloque_5_1_p);
  bloque_6 bloque_6_1 (
    .c0(or_2_out), .a0(X[12]), .b0(Y[12]), .a1(X[13]), .b1(Y[13]), .a2(X[14]), .b2(Y[14]), .a3(X[15]),
    .b3(Y[15]), .a4(X[16]), .b4(Y[16]), .a5(X[17]), .b5(Y[17]), .carry_bloque6(carry_out), .Ss(SUMA[17:12]));  // open: P

  // Other names for the same wires on the sheet: ss_3[2:0] = SUMA[2:0]; ss_4[3:0] = SUMA[6:3]; ss_5[4:0] = SUMA[11:7];
  //   ss_6[5:0] = SUMA[17:12]; x_17 = X[0]; x_16 = X[1]; x_15 = X[2]; x_14 = X[3]; x_13 = X[4]; x_12 = X[5];
  //   x_11 = X[6]; x_10 = X[7]; x_9 = X[8]; x_8 = X[9]; x_7 = X[10]; x_6 = X[11]; x_5 = X[12]; x_4 = X[13];
  //   x_3 = X[14]; x_2 = X[15]; x_1 = X[16]; x_0 = X[17]; y_17 = Y[0]; y_16 = Y[1]; y_15 = Y[2]; y_14 = Y[3];
  //   y_13 = Y[4]; y_12 = Y[5]; y_11 = Y[6]; y_10 = Y[7]; y_9 = Y[8]; y_8 = Y[9]; y_7 = Y[10]; y_6 = Y[11];
  //   y_5 = Y[12]; y_4 = Y[13]; y_3 = Y[14]; y_2 = Y[15]; y_1 = Y[16]; y_0 = Y[17]
endmodule

module bloque_3 (
  input  c0,
  input  a0,
  input  b0,
  input  a1,
  input  b1,
  input  a2,
  input  b2,
  output carry_bloque3,
  output [2:0] Ss,
  output P
);

  wire full_adder_2_1_c_out, full_adder_2_1_p, full_adder_2_2_c_out, full_adder_2_2_p, full_adder_2_3_p;

  FULL_ADDER_2 full_adder_2_1 (.A(a0), .B(b0), .C(c0), .P(full_adder_2_1_p), .S(Ss[0]), .C_OUT(full_adder_2_1_c_out));
  FULL_ADDER_2 full_adder_2_2 (
    .A(a1), .B(b1), .C(full_adder_2_1_c_out), .P(full_adder_2_2_p), .S(Ss[1]), .C_OUT(full_adder_2_2_c_out));
  FULL_ADDER_2 full_adder_2_3 (
    .A(a2), .B(b2), .C(full_adder_2_2_c_out), .P(full_adder_2_3_p), .S(Ss[2]), .C_OUT(carry_bloque3));
  and and_1 (P, full_adder_2_1_p, full_adder_2_3_p, full_adder_2_2_p);
endmodule

module bloque_4 (
  input  c0,
  input  a0,
  input  b0,
  input  a1,
  input  b1,
  input  a2,
  input  b2,
  input  a3,
  input  b3,
  output carry_bloque4,
  output [3:0] Ss,
  output P
);

  wire full_adder_2_1_c_out, full_adder_2_1_p, full_adder_2_2_c_out, full_adder_2_2_p, full_adder_2_3_c_out,
       full_adder_2_3_p, full_adder_2_4_p;

  FULL_ADDER_2 full_adder_2_1 (.A(a0), .B(b0), .C(c0), .P(full_adder_2_1_p), .S(Ss[0]), .C_OUT(full_adder_2_1_c_out));
  FULL_ADDER_2 full_adder_2_2 (
    .A(a1), .B(b1), .C(full_adder_2_1_c_out), .P(full_adder_2_2_p), .S(Ss[1]), .C_OUT(full_adder_2_2_c_out));
  FULL_ADDER_2 full_adder_2_3 (
    .A(a2), .B(b2), .C(full_adder_2_2_c_out), .P(full_adder_2_3_p), .S(Ss[2]), .C_OUT(full_adder_2_3_c_out));
  FULL_ADDER_2 full_adder_2_4 (
    .A(a3), .B(b3), .C(full_adder_2_3_c_out), .P(full_adder_2_4_p), .S(Ss[3]), .C_OUT(carry_bloque4));
  and and_1 (P, full_adder_2_1_p, full_adder_2_4_p, full_adder_2_3_p, full_adder_2_2_p);
endmodule

module FULL_ADDER_2 (
  input  A,
  input  B,
  input  C,
  output P,
  output S,
  output C_OUT
);

  wire and_1_out, and_2_out, or_1_out;

  xor xor_1 (P, A, B);
  or or_1 (or_1_out, A, B);
  and and_1 (and_1_out, B, A);
  xor xor_2 (S, P, C);
  and and_2 (and_2_out, C, or_1_out);
  or or_2 (C_OUT, and_2_out, and_1_out);
endmodule

module bloque_5 (
  input  c0,
  input  a0,
  input  b0,
  input  a1,
  input  b1,
  input  a2,
  input  b2,
  input  a3,
  input  b3,
  input  a4,
  input  b4,
  output carry_bloque6,
  output [4:0] Ss,
  output P
);

  wire full_adder_2_1_c_out, full_adder_2_1_p, full_adder_2_2_c_out, full_adder_2_2_p, full_adder_2_3_c_out,
       full_adder_2_3_p, full_adder_2_4_c_out, full_adder_2_4_p, full_adder_2_5_p;

  FULL_ADDER_2 full_adder_2_1 (.A(a0), .B(b0), .C(c0), .P(full_adder_2_1_p), .S(Ss[0]), .C_OUT(full_adder_2_1_c_out));
  FULL_ADDER_2 full_adder_2_2 (
    .A(a1), .B(b1), .C(full_adder_2_1_c_out), .P(full_adder_2_2_p), .S(Ss[1]), .C_OUT(full_adder_2_2_c_out));
  FULL_ADDER_2 full_adder_2_3 (
    .A(a2), .B(b2), .C(full_adder_2_2_c_out), .P(full_adder_2_3_p), .S(Ss[2]), .C_OUT(full_adder_2_3_c_out));
  FULL_ADDER_2 full_adder_2_4 (
    .A(a3), .B(b3), .C(full_adder_2_3_c_out), .P(full_adder_2_4_p), .S(Ss[3]), .C_OUT(full_adder_2_4_c_out));
  FULL_ADDER_2 full_adder_2_5 (
    .A(a4), .B(b4), .C(full_adder_2_4_c_out), .P(full_adder_2_5_p), .S(Ss[4]), .C_OUT(carry_bloque6));
  and and_1 (P, full_adder_2_1_p, full_adder_2_4_p, full_adder_2_5_p, full_adder_2_3_p, full_adder_2_2_p);
endmodule

module bloque_6 (
  input  c0,
  input  a0,
  input  b0,
  input  a1,
  input  b1,
  input  a2,
  input  b2,
  input  a3,
  input  b3,
  input  a4,
  input  b4,
  input  a5,
  input  b5,
  output carry_bloque6,
  output [5:0] Ss,
  output P
);

  wire full_adder_2_1_c_out, full_adder_2_1_p, full_adder_2_2_c_out, full_adder_2_2_p, full_adder_2_3_c_out,
       full_adder_2_3_p, full_adder_2_4_c_out, full_adder_2_4_p, full_adder_2_5_c_out, full_adder_2_5_p,
       full_adder_2_6_p;

  FULL_ADDER_2 full_adder_2_1 (.A(b0), .B(a0), .C(c0), .P(full_adder_2_1_p), .S(Ss[0]), .C_OUT(full_adder_2_1_c_out));
  FULL_ADDER_2 full_adder_2_2 (
    .A(a1), .B(b1), .C(full_adder_2_1_c_out), .P(full_adder_2_2_p), .S(Ss[1]), .C_OUT(full_adder_2_2_c_out));
  FULL_ADDER_2 full_adder_2_3 (
    .A(a2), .B(b2), .C(full_adder_2_2_c_out), .P(full_adder_2_3_p), .S(Ss[2]), .C_OUT(full_adder_2_3_c_out));
  FULL_ADDER_2 full_adder_2_4 (
    .A(a3), .B(b3), .C(full_adder_2_3_c_out), .P(full_adder_2_4_p), .S(Ss[3]), .C_OUT(full_adder_2_4_c_out));
  FULL_ADDER_2 full_adder_2_5 (
    .A(a4), .B(b4), .C(full_adder_2_4_c_out), .P(full_adder_2_5_p), .S(Ss[4]), .C_OUT(full_adder_2_5_c_out));
  FULL_ADDER_2 full_adder_2_6 (
    .A(a5), .B(b5), .C(full_adder_2_5_c_out), .P(full_adder_2_6_p), .S(Ss[5]), .C_OUT(carry_bloque6));
  and and_1 (P, full_adder_2_6_p, full_adder_2_1_p, full_adder_2_4_p, full_adder_2_5_p, full_adder_2_3_p, full_adder_2_2_p);
endmodule

module modo_alternativo (
  input  es_0,
  input  es_124,
  input  es_95,
  input  es_62,
  input  es_5,
  input  es_372,
  input  es_475,
  input  es_31,
  input  F1,
  input  F2,
  input  F3,
  input  F4,
  input  F5,
  output modo_alt
);

  wire f1y124_out, f2y95_out, f3y62_out, f4y5_out, f4y475_out, f5y31_out;

  and f1y124 (f1y124_out, es_124, F1);
  and f2y95 (f2y95_out, es_95, F2);
  and f3y62 (f3y62_out, es_62, F3);
  and f4y5 (f4y5_out, es_5, F4);
  and f4y475 (f4y475_out, es_475, F4);
  and f5y31 (f5y31_out, F5, es_31);
  or or_1 (modo_alt, f1y124_out, f2y95_out, f3y62_out, f4y475_out, f4y5_out, f5y31_out);
endmodule
